# Fritzing sketch portalbox-circuit (saved by Fritzing 0.9.3b)
breadboards: 1

parts:
  Composant1 = Arduino Uno (Rev3)
  LCD1 = LCD screen
  U1 = POT [package=3362u]
  R1 = Rotary Potentiometer (Small) [maximum_resistance=100kΩ package=THT]
  R2 = Rotary Potentiometer (Small) [maximum_resistance=100kΩ package=THT]
  R3 = Resistor [tolerance=±5% resistance=1k package=THT]
  R4 = Resistor [tolerance=±5% resistance=220 package="0603 [SMD]"]
  D1 = Rectifier Diode [part_number=1N4004 package="300 mil [THT]"]
  U2 = Voltage Regulator - 5V [part_number=TIP120 package="TO220 [THT]"]
  L1 = Solenoid
  J1 = Piezo Speaker

nets:
  N1: Composant1.A0, R1.wiper
  N2: Composant1.A1, R2.wiper
  N3: Composant1.D8, J1.pin2
  N4: Composant1.D9_PWM, R3.Pin_0, R3.Pin_1, U2.input_voltage
  N5: Composant1.D12/MISO, LCD1.E
  N6: Composant1.D13/SCK, LCD1.RS
  GND: Composant1.GND, LCD1.VSS, LCD1.R/W, LCD1.LED-, U1.E, R1.leg1, R2.leg1, U2.output_voltage, J1.pin1
  N7: Composant1.D4, LCD1.DB4
  N8: Composant1.D5_PWM, LCD1.DB5
  N9: Composant1.D6_PWM, LCD1.DB6
  N10: Composant1.D7, LCD1.DB7
  5V: Composant1.5V, LCD1.VDD, U1.A, R1.leg2, R2.leg2, R4.Pin_0, D1.cathode, L1.pin2
  N11: LCD1.V0, U1.S
  N12: LCD1.LED+, R4.Pin_1
  N13: D1.anode, U2.GND, L1.pin1
